# Fritzing sketch FullCircui (saved by Fritzing 0.9.3b)
breadboards: 1

parts:
  Part1 = Arduino Uno (Rev3) - ICSP
  LCD = Grove OLED 128x96
  Part2 = Barometric Pressure Sensor - BMP085 Breakout

nets:
  N1: Part1.A3, Part2.GND
  N2: Part1.A5/SCL, LCD.SCL, Part2.EOC
  N3: Part1.A4/SDA, LCD.SDA, Part2.XCLR
  N4: Part1.3V3, Part2.SDA
  5V: Part1.5V, LCD.VCC
  GND: Part1.GND, LCD.GND, Part2.SCL
